# Fritzing sketch car_veroboard_sketch (saved by Fritzing 0.9.3b)
perfboards: 1

parts:
  Part1 = Arduino Nano (Rev3.0) (ICSP)
  J1 = female pin header, 2 pins [form="♀ (female)"]
  J2 = female pin header, 2 pins [form="♀ (female)"]
  J3 = female pin header, 2 pins [form="♀ (female)"]
  J4 = female pin header, 2 pins [form="♀ (female)"]
  IC1 = L293D [package=THT]
  J5 = female pin header, 2 pins [form="♀ (female)"]

nets:
  N1: Part1.GND, IC1.0V
  N2: Part1.D2, J2.pin1
  N3: Part1.D3, J2.pin2
  N4: Part1.D4, J3.pin2
  N5: Part1.D5, J5.pin1
  N6: Part1.D6, J4.pin1
  N7: Part1.D7, J4.pin2
  N8: Part1.D8, IC1.In_3
  N9: Part1.D9, IC1.In_2
  N10: Part1.D10, IC1.Enable_1
  N11: Part1.D11/MOSI, IC1.In_1
  N12: Part1.D12/MISO, IC1.Enable_2
  N13: Part1.5V, J1.pin1, IC1.+V
  N14: Part1.D13/SCK, IC1.In_4
